# Fritzing sketch basic_controller (saved by Fritzing 0.8.7b)
breadboards: 1

parts:
  Part1 = Arduino Uno (Rev3) - ICSP
  xbee1 = Adafruit Xbee Adapter v1.1 [part_number=126]

nets:
  N1: Part1.ICSP_MOSI, Part1.D11_PWM/MOSI, xbee1.rx
  N2: Part1.D10_PWM/SS, xbee1.tx
  GND: Part1.GND, xbee1.gnd
  5V: Part1.5V, xbee1.+5v

custom parts:
  Adafruit Xbee Adapter v1.1: Adafruit Xbee Adapter
