# Fritzing sketch extended_controller (saved by Fritzing 0.8.7b)
breadboards: 1

parts:
  R1 = Resistor [tolerance=±5% resistance=100 package=THT]
  LED1 = LED - 5mm [color="Red (633nm)" package="5 mm [THT]"]
  Part1 = Arduino Uno (Rev3) - ICSP
  LED2 = LED - 5mm [color="Yellow (585nm)" package="5 mm [THT]"]
  LED3 = LED - 5mm [color="Green (570nm)" package="5 mm [THT]"]
  xbee1 = Adafruit Xbee Adapter v1.1 [part_number=126]

nets:
  GND: R1.Pin_0, Part1.GND, xbee1.gnd
  N1: R1.Pin_1, LED1.cathode, LED2.cathode, LED3.cathode
  N2: LED1.anode, Part1.D7
  N3: Part1.ICSP_MOSI, Part1.D11_PWM/MOSI, xbee1.rx
  N4: Part1.D10_PWM/SS, xbee1.tx
  N5: Part1.D5_PWM, LED3.anode
  N6: Part1.D6_PWM, LED2.anode
  5V: Part1.5V, xbee1.+5v

custom parts:
  Adafruit Xbee Adapter v1.1: Adafruit Xbee Adapter
